# Fritzing sketch invernadero_en_casa (saved by Fritzing 0.9.9b)
breadboards: 1

parts:
  VCC1 = Battery
  F1 = Fan - Ventilador [package=THT]
  Mod1 = KY-019 5V Relay Module [package="Breakout board"]
  Componente1 = FC-28 Soil Hygrometer Module - Probe
  Componente2 = FC-28 Soil Hygrometer Module
  M1 = DC Motor
  Mod2 = Heltec WiFi LoRa 32 V2 [part_number=HTIT-WB32LA]
  DHT1 = Humidity and Temperature Sensor DHT11
  LED1 = smd LED [color="Red (633nm)" package="1206 [SMD]"]
  LED2 = smd LED [color="Green (570nm)" package="1206 [SMD]"]
  R1 = Resistor [tolerance=±5% resistance=220 package="0603 [SMD]"]
  R2 = Resistor [tolerance=±5% resistance=220 package="2010 [SMD]"]

nets:
  N1: VCC1.+, Mod1.Common
  N2: F1.5V, Mod1.NO, M1.pin_2
  N3: F1.GND, M1.pin_1
  N4: Mod1.S, Mod2.pin_30
  N5: Mod1.+, Mod2.pin_20
  GND: Mod1.-, Componente2.GND, Mod2.GND, DHT1.GND_2
  N6: Componente1.POS, Componente2.POS
  N7: Componente1.NEG, Componente2.NEG
  VCC: Componente2.VCC, Mod2.pin_16, Mod2.pin_17, DHT1.Vcc
  N8: Componente2.AO, Mod2.pin_33
  N9: Mod2.pin_2, DHT1.Data-signal
  N10: Mod2.pin_21, Mod2.pin_22
  N11: LED1.cathode, R2.Pin_1
  N12: LED2.cathode, R1.Pin_1

custom parts:
  Battery: Your standard 2x 18650 battery pack (14.7 Volts)
  Fan - Ventilador: Ventilador de 2 pines, se encuentra comunmente en computadoras de escritorio
  KY-019 5V Relay Module: KY-019 5V Relay module, used to control AC circuits. (Special thanks to vanepp for fixing the PCB holes and other errors)
  FC-28 Soil Hygrometer Module - Probe: The FC-28 is a soil hygrometer module that uses the Texas Instruments LM393 comparator chip to provide an analog measurement of soil humidity.
  FC-28 Soil Hygrometer Module: The FC-28 is a soil hygrometer module that uses the Texas Instruments LM393 comparator chip to provide an analog measurement of soil humidity. The digital output is high when soil moisture is over a certain threshold, as determined by adjusting the potentiometer.
  Humidity and Temperature Sensor DHT11: Digital relative humidity & temperature sensor DHT11
